# Fritzing sketch wire-diagram (saved by Fritzing 0.9.5d)
breadboards: 1

parts:
  Part1 = Arduino Uno (Rev3) - ICSP
  Part2 = OLED Monochrome 128x32 I2C [part_number=931]
  SW1 = ENCODER_RGB_CA [package=encoder_led_3]

nets:
  N1: Part1.A4/SDA, Part2.SDA
  N2: Part1.A5/SCL, Part2.SCL
  N3: Part1.D2, SW1.B
  N4: Part1.D3_PWM, SW1.A
  N5: Part1.D4, SW1.+
  5V: Part1.5V, Part2.VIN, SW1.-R
  GND: Part1.GND, Part2.GND, SW1.-G

custom parts:
  OLED Monochrome 128x32 I2C: These displays are small, only about 1" diagonal, but very readable due to the high contrast of an OLED display. This display is made of 128x32 individual white OLED pixels, each one is turned on or off by the controller chip. Because the display makes its own light, no backlight is required. This reduces the power required to run the OLED and is why the display has such high contrast; we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
